# Fritzing sketch WearableHMS_Schema (saved by Fritzing 0.9.4)
breadboards: 1

parts:
  Mod1 = gy-906
  M1 = MakerFocus MAX30102
  M2 = Grove GSR Sensor
  Part1 = Arduino Nano (Rev3.0)
  Part2 = InvenSense MPU6050

nets:
  VIN: Mod1.VIN, M1.VIN, M2.VCC, Part1.3V3, Part2.VCC
  GND: Mod1.GND, M1.GND, M2.GND, Part1.GND, Part2.GND
  N1: Mod1.SCL, M1.SCL, Part1.A5, Part2.SCL
  N2: Mod1.SDA, M1.SDA, Part1.A4, Part2.SDA
  N3: M2.SIG, Part1.A1

custom parts:
  gy-906: gy-906 Non-contact PIR I2C interface temperature sensor breakout board.
  MakerFocus MAX30102: Oximeter module using the MAX30102 chip. As usual, if you want the mounting holes in pcb, you need to drag a hole over the pad in silkscreen to actually drill the hole (by default they are not drilled)
  Grove GSR Sensor: GSR stands for galvanic skin response, is a method of measuring the electrical conductance of the skin. Strong emotion can cause stimulus to your sympathetic nervous system, resulting more sweat being secreted by the sweat glands.
